// Logisim project CPU.circ as structural Verilog: 5 circuits, main circuit CPU
module CPU (
);

  wire clock_1_out, OE, OW, por_1_out, processor_1_load_on, processor_1_rom_b, processor_1_sram;
  wire [3:0] controlled_buffer_1_out, counter_1_q, processor_1_addr_ram, processor_1_load_rom,
       processor_1_ra, processor_1_ram_out, processor_1_rb, ram_1_dout, register_1_q, rom_1_data;

  Clock clock_1 (.out(clock_1_out));
  Counter #(.max('hf), .width(4)) counter_1 (
    .load(processor_1_load_on), .D(processor_1_load_rom), .Q(counter_1_q), .clk(clock_1_out), .clr(por_1_out));  // open: count, carry, up
  assign controlled_buffer_1_out = processor_1_rom_b ? counter_1_q : 4'bz;  // Controlled_Buffer controlled_buffer_1
  Pull_Resistor pull_resistor_1 (.node(controlled_buffer_1_out));
  ROM #(.addrWidth(4), .dataWidth(4)) rom_1 (.addr(controlled_buffer_1_out), .data(rom_1_data));
  Hex_Digit_Display RA (.value(processor_1_ra));  // open: dp
  Hex_Digit_Display RB (.value(processor_1_rb));  // open: dp
  Hex_Digit_Display OUT_RAM (.value(register_1_q));  // open: dp
  POR #(.PorHighDuration(1)) por_1 (.out(por_1_out));
  RAM #(.addrWidth(4), .asyncread("true"), .dataWidth(4)) ram_1 (
    .addr(processor_1_addr_ram), .we(OW), .oe(OE), .clk(clock_1_out), .din(processor_1_ram_out),
    .dout(ram_1_dout));
  Processor processor_1 (
    .ROM(rom_1_data), .R(por_1_out), .CLK(clock_1_out), .RAM_INPUT(ram_1_dout),
    .RAM_OUT(processor_1_ram_out), .RA(processor_1_ra), .RB(processor_1_rb), .ADDR_RAM(processor_1_addr_ram),
    .ROM_B(processor_1_rom_b), .RAM_OW(OE), .SRAM(processor_1_sram), .RAM_RW(OW),
    .LOAD_ROM(processor_1_load_rom), .LOAD_ON(processor_1_load_on));
  Pull_Resistor pull_resistor_2 (.node(ram_1_dout));
  Register #(.width(4)) register_1 (
    .D(ram_1_dout), .en(processor_1_sram), .clk(clock_1_out), .Q(register_1_q), .clr(por_1_out));
endmodule

module Processor (
  input  [3:0] ROM,
  input  R,
  input  CLK,
  input  [3:0] RAM_INPUT,
  output [3:0] RAM_OUT,
  output [3:0] RA,
  output [3:0] RB,
  output [3:0] ADDR_RAM,
  output ROM_B,
  output RAM_OW,
  output SRAM,
  output RAM_RW,
  output [3:0] LOAD_ROM,
  output LOAD_ON
);

  wire alu_1_ram_we, and_1_out, or_1_out, or_2_out, pla_4_out, rgs_1_ram_ow, shift_register_1_p1,
       shift_register_1_p3, shift_register_2_p1;
  wire [1:0] pla_2_out, pla_5_out;
  wire [3:0] alu_1_result, controlled_buffer_1_out, controlled_buffer_2_out, fde_1_arg, fde_1_opcode,
       rgs_1_ra_out, rgs_1_ram_out, rgs_1_rb_out;

  // Shift_Register #(.length(1), .parallel("false")) shift_register_1: pin names not known; wires that end beside it: shift_register_1_p1, CLK, shift_register_1_p3
  and and_1 (and_1_out, CLK, or_1_out);
  or or_1 (or_1_out, R, ROM_B);
  S_R_Flip_Flop s_r_ff_1 (.clk(CLK), .reset(R), .Qn(ROM_B), .preset(shift_register_1_p1));  // open: S, R, Q
  FDE fde_1 (.ROM(ROM), .R(R), .CLK(and_1_out), .opcode(fde_1_opcode), .arg(fde_1_arg));
  PLA #(.in_width(4), .out_width(1), .\table ("1111 1 # HALT")) pla_1 (.in(fde_1_opcode), .out(shift_register_1_p3));
  PLA #(.in_width(4), .\table ("1100 01 # SHOW RA\n1101 10 # SHOW RB")) pla_2 (.in(ROM), .out(pla_2_out));
  PLA #(.in_width(4), .out_width(1), .\table ("1110 1 # SHOW RAM")) pla_3 (.in(fde_1_opcode), .out(SRAM));
  PLA #(.in_width(4), .out_width(1), .\table ("1011 1 # JMP")) pla_4 (.in(ROM), .out(pla_4_out));
  PLA #(.in_width(4), .\table ("0101 01 # MOV RA -> RAM\n0111 01 # MOV RB -> RAM\n1001 01 # ALU\n0110 10 # MOV RAM -> RA\n1000 10 # MOV RAM -> RB")) pla_5 (
    .in(fde_1_opcode), .out(pla_5_out));
  assign controlled_buffer_1_out = SRAM ? fde_1_arg : 4'bz;  // Controlled_Buffer controlled_buffer_1
  or or_2 (or_2_out, pla_5_out[1], pla_5_out[0]);
  assign controlled_buffer_2_out = or_2_out ? fde_1_arg : 4'bz;  // Controlled_Buffer controlled_buffer_2
  Pull_Resistor pull_resistor_1 (.node(controlled_buffer_1_out));
  assign LOAD_ROM = LOAD_ON ? fde_1_arg : 4'bz;  // Controlled_Buffer controlled_buffer_3
  RGS rgs_1 (
    .opcode(fde_1_opcode), .arg(fde_1_arg), .R(R), .RAM_INPUT(RAM_INPUT), .CLK(and_1_out),
    .RAM_OW(rgs_1_ram_ow), .RAM_OUT(rgs_1_ram_out), .RA_OUT(rgs_1_ra_out), .RB_OUT(rgs_1_rb_out));
  ALU alu_1 (
    .opcode(fde_1_opcode), .RA_IN(rgs_1_ra_out), .RB_IN(rgs_1_rb_out), .RAM_WE(alu_1_ram_we),
    .RESULT(alu_1_result));
  assign ADDR_RAM = controlled_buffer_2_out | controlled_buffer_1_out;  // OR_Gate or_3, 4 bits wide
  or or_4 (RAM_OW, pla_5_out[1], SRAM);
  // Shift_Register #(.length(1), .parallel("false")) shift_register_2: pin names not known; wires that end beside it: shift_register_2_p1, shift_register_2_p1, R, CLK, pla_4_out, LOAD_ON
  assign RAM_OUT = rgs_1_ram_out | alu_1_result;  // OR_Gate or_5, 4 bits wide
  Pull_Resistor pull_resistor_2 (.node(LOAD_ROM));
  Pull_Resistor pull_resistor_3 (.node(controlled_buffer_2_out));
  or or_6 (RAM_RW, alu_1_ram_we, rgs_1_ram_ow);
  Register #(.width(4)) register_1 (.D(rgs_1_ra_out), .en(pla_2_out[0]), .clk(and_1_out), .Q(RA), .clr(R));
  Register #(.width(4)) register_2 (.D(rgs_1_rb_out), .en(pla_2_out[1]), .clk(and_1_out), .Q(RB), .clr(R));
endmodule

module FDE (
  input  [3:0] ROM,
  input  R,
  input  CLK,
  output [3:0] opcode,
  output [3:0] arg
);

  wire and_1_out, d_ff_1_q, or_2_out, or_4_out, pla_1_out, pla_2_out, s_r_ff_1_q, s_r_ff_1_qn,
       shift_register_1_p3;
  wire [3:0] controlled_buffer_1_out, controlled_buffer_2_out, IR_q;

  PLA #(.in_width(4), .out_width(1), .\table ("0011 1 # MOV RA -> RB\n0100 1 # MOV RB -> RA\n1100 1 # SHOW RA\n1101 1 # SHOW RB\n1111 1 # HALT")) pla_1 (
    .in(ROM), .out(pla_1_out));
  PLA #(.in_width(4), .out_width(1), .\table ("0001 1 # SET RA\n0010 1 # SET RB\n0101 1 # MOV RA -> RAM\n0110 1 # MOV RAM -> RA\n0111 1 # MOV RB -> RAM\n1000 1 # MOV RAM -> RB\n1001 1 # ADD RA, RB -> RAM\n1010 1 # SUB RA, RB -> RAM\n1011 1 # JMP\n1110 1 # SHOW RAM")) pla_2 (
    .in(ROM), .out(pla_2_out));
  D_Flip_Flop d_ff_1 (.D(pla_2_out), .clk(CLK), .Q(d_ff_1_q), .reset(R));  // open: Qn, preset
  // Shift_Register #(.length(2), .parallel("false")) shift_register_1: pin names not known; wires that end beside it: CLK, pla_2_out, shift_register_1_p3
  // OR_Gate or_1 has open pins: in0=shift_register_1_p3, in1=R, out=open
  S_R_Flip_Flop s_r_ff_1 (
    .clk(CLK), .Q(s_r_ff_1_q), .reset(or_2_out), .Qn(s_r_ff_1_qn), .preset(d_ff_1_q));  // open: S, R
  or or_2 (or_2_out, R, shift_register_1_p3);
  assign controlled_buffer_1_out = and_1_out ? ROM : 4'bz;  // Controlled_Buffer controlled_buffer_1
  and and_1 (and_1_out, pla_1_out, s_r_ff_1_qn);
  Register #(.width(4)) IR (.D(ROM), .en(pla_2_out), .clk(CLK), .Q(IR_q), .clr(or_4_out));
  Pull_Resistor pull_resistor_1 (.node(controlled_buffer_1_out));
  assign opcode = controlled_buffer_1_out | controlled_buffer_2_out;  // OR_Gate or_3, 4 bits wide
  assign controlled_buffer_2_out = s_r_ff_1_q ? IR_q : 4'bz;  // Controlled_Buffer controlled_buffer_2
  or or_4 (or_4_out, R, shift_register_1_p3);
  assign arg = s_r_ff_1_q ? ROM : 4'bz;  // Controlled_Buffer controlled_buffer_3
  Pull_Resistor pull_resistor_2 (.node(controlled_buffer_2_out));
  Pull_Resistor pull_resistor_3 (.node(arg));
endmodule

module RGS (
  input  [3:0] opcode,
  input  [3:0] arg,
  input  R,
  input  [3:0] RAM_INPUT,
  input  CLK,
  output RAM_OW,
  output [3:0] RAM_OUT,
  output [3:0] RA_OUT,
  output [3:0] RB_OUT
);

  wire demultiplexer_1_out1, demultiplexer_1_out2, demultiplexer_1_out3, demultiplexer_1_out4,
       demultiplexer_1_out5, demultiplexer_1_out6, demultiplexer_1_out7, demultiplexer_1_out8, nor_1_out,
       nor_2_out, or_3_out, or_4_out;
  wire [3:0] controlled_buffer_3_out, controlled_buffer_7_out, or_1_out, or_2_out, pull_resistor_1_node,
       pull_resistor_2_node, pull_resistor_3_node, pull_resistor_4_node, pull_resistor_6_node;

  Demultiplexer #(.select(4)) demultiplexer_1 (
    .out1(demultiplexer_1_out1), .out2(demultiplexer_1_out2), .out3(demultiplexer_1_out3),
    .out4(demultiplexer_1_out4), .out5(demultiplexer_1_out5), .out6(demultiplexer_1_out6),
    .out7(demultiplexer_1_out7), .out8(demultiplexer_1_out8), .in(1'b1), .sel(opcode));  // open: out0, out9, out10, out11, out12, out13, out14, out15
  nor nor_1 (nor_1_out, demultiplexer_1_out1, demultiplexer_1_out2);
  nor nor_2 (nor_2_out, nor_1_out, demultiplexer_1_out8, demultiplexer_1_out3, demultiplexer_1_out4, demultiplexer_1_out5, demultiplexer_1_out6, demultiplexer_1_out7);
  Pull_Resistor pull_resistor_1 (.node(pull_resistor_1_node));
  Pull_Resistor pull_resistor_2 (.node(pull_resistor_2_node));
  assign pull_resistor_2_node = nor_2_out ? arg : 4'bz;  // Controlled_Buffer controlled_buffer_1
  assign pull_resistor_1_node = demultiplexer_1_out6 ? RAM_INPUT : 4'bz;  // Controlled_Buffer controlled_buffer_2
  assign controlled_buffer_3_out = demultiplexer_1_out8 ? RAM_INPUT : 4'bz;  // Controlled_Buffer controlled_buffer_3
  Pull_Resistor pull_resistor_3 (.node(pull_resistor_3_node));
  assign pull_resistor_3_node = demultiplexer_1_out4 ? RB_OUT : 4'bz;  // Controlled_Buffer controlled_buffer_4
  Pull_Resistor pull_resistor_4 (.node(pull_resistor_4_node));
  assign pull_resistor_4_node = demultiplexer_1_out3 ? RA_OUT : 4'bz;  // Controlled_Buffer controlled_buffer_5
  Pull_Resistor pull_resistor_5 (.node(controlled_buffer_3_out));
  assign or_1_out = pull_resistor_2_node | pull_resistor_3_node | pull_resistor_1_node;  // OR_Gate or_1, 4 bits wide
  assign or_2_out = pull_resistor_2_node | pull_resistor_4_node | controlled_buffer_3_out;  // OR_Gate or_2, 4 bits wide
  Register #(.width(4)) RA (.D(or_1_out), .en(or_3_out), .clk(CLK), .Q(RA_OUT), .clr(R));
  or or_3 (or_3_out, demultiplexer_1_out1, demultiplexer_1_out4, demultiplexer_1_out6);
  Register #(.width(4)) RB (.D(or_2_out), .en(or_4_out), .clk(CLK), .Q(RB_OUT), .clr(R));
  or or_4 (or_4_out, demultiplexer_1_out2, demultiplexer_1_out3, demultiplexer_1_out8);
  or or_5 (RAM_OW, demultiplexer_1_out5, demultiplexer_1_out7);
  Pull_Resistor pull_resistor_6 (.node(pull_resistor_6_node));
  assign pull_resistor_6_node = demultiplexer_1_out5 ? RA_OUT : 4'bz;  // Controlled_Buffer controlled_buffer_6
  assign RAM_OUT = pull_resistor_6_node | controlled_buffer_7_out;  // OR_Gate or_6, 4 bits wide
  assign controlled_buffer_7_out = demultiplexer_1_out7 ? RB_OUT : 4'bz;  // Controlled_Buffer controlled_buffer_7
  Pull_Resistor pull_resistor_7 (.node(controlled_buffer_7_out));
endmodule

module ALU (
  input  [3:0] opcode,
  input  [3:0] RA_IN,
  input  [3:0] RB_IN,
  output RAM_WE,
  output [3:0] RESULT
);

  wire pla_1_out, pla_2_out;
  wire [3:0] adder_1_out, controlled_buffer_2_out, controlled_buffer_3_out, controlled_buffer_4_out,
       pull_resistor_1_node, subtractor_1_out;

  PLA #(.in_width(4), .out_width(1), .\table ("1010 1 # SUB RA RB")) pla_1 (.in(opcode), .out(pla_1_out));
  PLA #(.in_width(4), .out_width(1), .\table ("1001 1 # ADD RA RB")) pla_2 (.in(opcode), .out(pla_2_out));
  Pull_Resistor pull_resistor_1 (.node(pull_resistor_1_node));
  assign pull_resistor_1_node = pla_2_out ? RB_IN : 4'bz;  // Controlled_Buffer controlled_buffer_1
  assign controlled_buffer_2_out = pla_2_out ? RA_IN : 4'bz;  // Controlled_Buffer controlled_buffer_2
  assign controlled_buffer_3_out = pla_1_out ? RA_IN : 4'bz;  // Controlled_Buffer controlled_buffer_3
  assign controlled_buffer_4_out = pla_1_out ? RB_IN : 4'bz;  // Controlled_Buffer controlled_buffer_4
  Pull_Resistor pull_resistor_2 (.node(controlled_buffer_4_out));
  or or_1 (RAM_WE, pla_2_out, pla_1_out);
  Adder #(.width(4)) adder_1 (
    .a(pull_resistor_1_node), .b(controlled_buffer_2_out), .out(adder_1_out));  // open: cin, cout
  Pull_Resistor pull_resistor_3 (.node(controlled_buffer_2_out));
  Pull_Resistor pull_resistor_4 (.node(controlled_buffer_3_out));
  Subtractor #(.width(4)) subtractor_1 (
    .a(controlled_buffer_3_out), .b(controlled_buffer_4_out), .out(subtractor_1_out));  // open: bin, bout
  assign RESULT = adder_1_out | subtractor_1_out;  // OR_Gate or_2, 4 bits wide
endmodule
